// Logisim project Practica 2.circ as structural Verilog: 1 circuit, main circuit main
module main (
  input  A,
  input  in_2,
  input  A_2,
  input  B,
  input  in_5,
  input  A_3,
  input  B_2,
  input  in_8,
  input  A_4,
  input  B_3,
  input  Llave,
  input  Switch,
  input  Sensor,
  input  X1,
  input  X2,
  input  Y1,
  input  Y2,
  input  A_5,
  input  B_4,
  input  C,
  input  D,
  output out_22,
  output out_23,
  output out_24,
  output out_25,
  output out_26,
  output X___Y,
  output X___Y_2,
  output X___Y_3,
  output out_30
);

  wire and_1_out, and_2_out, and_3_out, and_4_out, and_5_out, and_6_out, and_7_out, and_8_out, and_9_out,
       and_10_out, and_11_out, and_12_out, and_13_out, and_14_out, and_15_out, and_16_out, and_17_out,
       not_1_out, not_2_out, not_3_out, not_4_out, not_5_out, not_7_out, not_8_out, not_9_out, not_10_out,
       transistor_1_out, transistor_2_out, transistor_4_out, transistor_7_out, transistor_8_out;

  Transistor transistor_1 (.in(1'b1), .out(transistor_1_out), .gate(A_4));
  Transistor transistor_2 (.in(1'b1), .out(transistor_2_out), .gate(B_3));
  not not_1 (not_1_out, X1);
  not not_2 (not_2_out, X2);
  not not_3 (not_3_out, Y1);
  not not_4 (not_4_out, Y2);
  not not_5 (not_5_out, A_5);
  // NOT_Gate not_6 has open pins: in=B_4, out=open
  not not_7 (not_7_out, C);
  not not_8 (not_8_out, D);
  Transistor transistor_3 (.in(in_2), .out(out_22), .gate(A));
  Transistor #(.\type ("n")) transistor_4 (.in(in_5), .out(transistor_4_out), .gate(B));
  Transistor #(.\type ("n")) transistor_5 (.in(in_8), .out(out_24), .gate(A_3));
  Transistor #(.\type ("n")) transistor_6 (.in(in_8), .out(out_24), .gate(B_2));
  Transistor #(.\type ("n")) transistor_7 (.in(1'b1), .out(transistor_7_out), .gate(B_3));
  Transistor #(.\type ("n")) transistor_8 (.in(1'b1), .out(transistor_8_out), .gate(A_4));
  not not_9 (not_9_out, Switch);
  not not_10 (not_10_out, Sensor);
  Transistor #(.\type ("n")) transistor_9 (.in(transistor_4_out), .out(out_23), .gate(A_2));
  Transistor #(.\type ("n")) transistor_10 (.in(transistor_7_out), .out(out_25), .gate(transistor_1_out));
  Transistor #(.\type ("n")) transistor_11 (.in(transistor_8_out), .out(out_25), .gate(transistor_2_out));
  and and_1 (and_1_out, Llave, not_9_out, Sensor);
  and and_2 (and_2_out, Llave, Switch, not_10_out);
  and and_3 (and_3_out, B_4, not_7_out);
  and and_4 (and_4_out, A_5, not_7_out);
  and and_5 (and_5_out, not_5_out, not_7_out, not_8_out);
  and and_6 (and_6_out, A_5, B_4, C);
  and and_7 (and_7_out, A_5, C, not_8_out);
  or or_1 (out_26, and_1_out, and_2_out);
  and and_8 (and_8_out, not_1_out, Y1);
  and and_9 (and_9_out, not_1_out, not_2_out, Y2);
  and and_10 (and_10_out, not_2_out, Y1, Y2);
  and and_11 (and_11_out, X1, not_3_out);
  and and_12 (and_12_out, X2, not_3_out, not_4_out);
  and and_13 (and_13_out, X1, X2, not_4_out);
  and and_14 (and_14_out, not_1_out, not_2_out, not_3_out, not_4_out);
  and and_15 (and_15_out, not_1_out, X2, not_3_out, Y2);
  and and_16 (and_16_out, X1, X2, Y2, Y1);
  and and_17 (and_17_out, X1, not_2_out, Y1, not_4_out);
  or or_2 (X___Y, and_8_out, and_9_out, and_10_out);
  or or_3 (X___Y_2, and_11_out, and_12_out, and_13_out);
  or or_4 (X___Y_3, and_14_out, and_15_out, and_16_out, and_17_out);
  or or_5 (out_30, and_3_out, and_4_out, and_5_out, and_6_out, and_7_out);

  // Notes on the sheet:
  //   Puerta inteligente
  //   NOT
  //   Comparador de 2 bits
  //   Tabla de verdad misteriora
  //   AND
  //   OR
  //   XOR
  //   ¬X1 y Y1
  //   ¬(X1X2) y Y2
  //   ¬X2 y Y1Y2
  //   X1 y ¬Y1
  //   X2 y ¬(Y1Y2)
  //   X1X2 y ¬Y2
  //   ¬(X1X2) y ¬(Y1Y2)
  //   (¬X1)X2 y (¬Y1)Y2
  //   X1X2 y Y1Y2
  //   X1(¬X2) y Y1(¬Y2)
  //   B y ¬C
  //   A y ¬C
  //   ¬A y ¬(CD)
  //   AB y C
  //   A y C(¬D)
endmodule
