// Logisim project Practica 3.circ as structural Verilog: 5 circuits, main circuit ALU
module Add_1_bit (
  input  in_1,
  input  A,
  input  B,
  output Suma,
  output out_5
);

  wire and_1_out, and_2_out, xor_1_out;

  xor xor_1 (xor_1_out, A, B);
  and and_1 (and_1_out, A, B);
  xor xor_2 (Suma, in_1, xor_1_out);
  and and_2 (and_2_out, in_1, xor_1_out);
  xor xor_3 (out_5, and_2_out, and_1_out);

  // Notes on the sheet:
  //   Acarreo de entrada
  //   Acarreo de salida
endmodule

module Full_Adder_8_bits (
  input  in_1,
  input  [7:0] in_2,
  input  [7:0] in_3,
  output [7:0] out_4,
  output out_5
);

  wire add_1_bit_1_out_5, add_1_bit_2_out_5, add_1_bit_3_out_5, add_1_bit_4_out_5, add_1_bit_5_out_5,
       add_1_bit_6_out_5, add_1_bit_7_out_5;

  Add_1_bit add_1_bit_1 (.in_1(in_1), .A(in_2[0]), .B(in_3[0]), .Suma(out_4[0]), .out_5(add_1_bit_1_out_5));
  Add_1_bit add_1_bit_2 (
    .in_1(add_1_bit_1_out_5), .A(in_2[1]), .B(in_3[1]), .Suma(out_4[1]), .out_5(add_1_bit_2_out_5));
  Add_1_bit add_1_bit_3 (
    .in_1(add_1_bit_2_out_5), .A(in_2[2]), .B(in_3[2]), .Suma(out_4[2]), .out_5(add_1_bit_3_out_5));
  Add_1_bit add_1_bit_4 (
    .in_1(add_1_bit_3_out_5), .A(in_2[3]), .B(in_3[3]), .Suma(out_4[3]), .out_5(add_1_bit_4_out_5));
  Add_1_bit add_1_bit_5 (
    .in_1(add_1_bit_4_out_5), .A(in_2[4]), .B(in_3[4]), .Suma(out_4[4]), .out_5(add_1_bit_5_out_5));
  Add_1_bit add_1_bit_6 (
    .in_1(add_1_bit_5_out_5), .A(in_2[5]), .B(in_3[5]), .Suma(out_4[5]), .out_5(add_1_bit_6_out_5));
  Add_1_bit add_1_bit_7 (
    .in_1(add_1_bit_6_out_5), .A(in_2[6]), .B(in_3[6]), .Suma(out_4[6]), .out_5(add_1_bit_7_out_5));
  Add_1_bit add_1_bit_8 (.in_1(add_1_bit_7_out_5), .A(in_2[7]), .B(in_3[7]), .Suma(out_4[7]), .out_5(out_5));

  // Notes on the sheet:
  //   Acarreo de entrada
  //   A
  //   B
  //   Resultado
  //   Acarreo de salida
endmodule

module Full_Adder_4_bits (
  input  in_1,
  input  [3:0] A,
  input  [3:0] B,
  output [3:0] Resultado,
  output out_5
);

  wire add_1_bit_1_out_5, add_1_bit_2_out_5, add_1_bit_3_out_5;

  Add_1_bit add_1_bit_1 (.in_1(in_1), .A(A[0]), .B(B[0]), .Suma(Resultado[0]), .out_5(add_1_bit_1_out_5));
  Add_1_bit add_1_bit_2 (.in_1(add_1_bit_1_out_5), .A(A[1]), .B(B[1]), .Suma(Resultado[1]), .out_5(add_1_bit_2_out_5));
  Add_1_bit add_1_bit_3 (.in_1(add_1_bit_2_out_5), .A(A[2]), .B(B[2]), .Suma(Resultado[2]), .out_5(add_1_bit_3_out_5));
  Add_1_bit add_1_bit_4 (.in_1(add_1_bit_3_out_5), .A(A[3]), .B(B[3]), .Suma(Resultado[3]), .out_5(out_5));

  // Notes on the sheet:
  //   Acarreo de entrada
  //   Acarreo de salida
endmodule

module ALU (
  input  [3:0] A,
  input  [3:0] B,
  input  [2:0] in_3,
  output Zero,
  output Overflow,
  output Negative,
  output _0__Logica,
  output [3:0] Resultado
);

  wire and_2_out, full_adder_4_bits_1_out_5, full_adder_4_bits_2_out_5, not_2_out, or_3_out;
  wire [3:0] and_1_out, full_adder_4_bits_1_resultado, full_adder_4_bits_2_resultado, not_1_out, or_1_out,
       sub_4_bits_1_resultado, sub_4_bits_2_resultado;

  Full_Adder_4_bits full_adder_4_bits_1 (
    .in_1(1'b0), .A(A), .B(B), .Resultado(full_adder_4_bits_1_resultado), .out_5(full_adder_4_bits_1_out_5));
  Sub_4_bits sub_4_bits_1 (.in_1(1'b1), .A(A), .B(B), .Resultado(sub_4_bits_1_resultado));  // open: out_5
  Full_Adder_4_bits full_adder_4_bits_2 (
    .in_1(1'b0), .A(A), .B(4'b0001), .Resultado(full_adder_4_bits_2_resultado),
    .out_5(full_adder_4_bits_2_out_5));
  Sub_4_bits sub_4_bits_2 (.in_1(1'b1), .A(A), .B(4'b0001), .Resultado(sub_4_bits_2_resultado));  // open: out_5
  assign or_1_out = A | B;  // OR_Gate or_1, 4 bits wide
  assign and_1_out = A & B;  // AND_Gate and_1, 4 bits wide
  assign not_1_out = ~A;  // NOT_Gate not_1, 4 bits wide
  Multiplexer #(.select(3), .width(4), .enable("false")) multiplexer_1 (
    .in0(and_1_out), .in1(or_1_out), .in2(full_adder_4_bits_1_resultado), .in3(sub_4_bits_1_resultado),
    .in4(not_1_out), .in5(full_adder_4_bits_2_resultado), .in6(sub_4_bits_2_resultado), .in7(A),
    .out(Resultado), .sel(in_3));
  not not_2 (not_2_out, in_3[2]);
  or or_2 (Overflow, full_adder_4_bits_1_out_5, full_adder_4_bits_2_out_5);
  and and_2 (and_2_out, in_3[0], in_3[1], not_2_out);
  or or_3 (or_3_out, Resultado[0], Resultado[1], Resultado[2], Resultado[3]);
  or or_4 (_0__Logica, in_3[1], in_3[2]);
  not not_3 (Zero, or_3_out);
  and and_3 (Negative, Resultado[3], and_2_out);

  // Notes on the sheet:
  //   Operación
  //   000. AND
  //   001. OR
  //   010. ADD
  //   011. SUB
  //   100. NEGATE
  //   101. INCREMENT
  //   110. DECREMENT
  //   111. PASS
  //   1. Aritmetica
endmodule

module Sub_4_bits (
  input  in_1,
  input  [3:0] A,
  input  [3:0] B,
  output [3:0] Resultado,
  output out_5
);

  wire add_1_bit_1_out_5, add_1_bit_2_out_5, add_1_bit_3_out_5, not_1_out, not_2_out, not_3_out, not_4_out;

  not not_1 (not_1_out, B[0]);
  not not_2 (not_2_out, B[1]);
  not not_3 (not_3_out, B[2]);
  not not_4 (not_4_out, B[3]);
  Add_1_bit add_1_bit_1 (.in_1(in_1), .A(A[0]), .B(not_1_out), .Suma(Resultado[0]), .out_5(add_1_bit_1_out_5));
  Add_1_bit add_1_bit_2 (
    .in_1(add_1_bit_1_out_5), .A(A[1]), .B(not_2_out), .Suma(Resultado[1]), .out_5(add_1_bit_2_out_5));
  Add_1_bit add_1_bit_3 (
    .in_1(add_1_bit_2_out_5), .A(A[2]), .B(not_3_out), .Suma(Resultado[2]), .out_5(add_1_bit_3_out_5));
  Add_1_bit add_1_bit_4 (.in_1(add_1_bit_3_out_5), .A(A[3]), .B(not_4_out), .Suma(Resultado[3]), .out_5(out_5));

  // Notes on the sheet:
  //   Acarreo de entrada
  //   Acarreo de salida
endmodule
