// Logisim project Practica9(MIO).circ as structural Verilog: 3 circuits, main circuit main
module main (
  input  [7:0] \Dirección ,
  input  [7:0] Entrada,
  input  Reloj,
  input  Salida,
  input  _0___RAM,
  input  [7:0] \Dirección_2 ,
  input  in_7,
  output [7:0] out_8,
  output [7:0] Datos_de_lectura,
  output [7:0] out_10
);

  ROM rom_1 (.addr(\Dirección_2 ), .data(out_10), .sel(in_7));
  RAM #(.bus("separate")) ram_1 (
    .addr(\Dirección ), .din(Entrada), .data(out_8), .clk(Reloj), .ld(Salida));  // open: str, sel, clr
  Multiplexer #(.width(8)) multiplexer_1 (
    .in0(out_8), .in1(out_10), .out(Datos_de_lectura), .sel(_0___RAM));  // open: en

  // Notes on the sheet:
  //   1 = ROM
endmodule

module Control_Unit (
  input  [7:0] \Codigo_de_operación ,
  output [8:0] Codigo_de_Cu
);

  wire comparator_1_eq, comparator_2_eq, comparator_3_eq, comparator_4_eq;
  wire [2:0] multiplexer_1_out, multiplexer_2_out, multiplexer_3_out, multiplexer_4_out, or_1_out;

  Comparator comparator_1 (.a(\Codigo_de_operación ), .b(8'h3), .eq(comparator_1_eq));  // open: gt, lt
  Comparator comparator_2 (.a(\Codigo_de_operación ), .b(8'h23), .eq(comparator_2_eq));  // open: gt, lt
  Comparator comparator_3 (.a(\Codigo_de_operación ), .b(8'h33), .eq(comparator_3_eq));  // open: gt, lt
  Comparator comparator_4 (.a(\Codigo_de_operación ), .b(8'h63), .eq(comparator_4_eq));  // open: gt, lt
  Multiplexer #(.width(3)) multiplexer_1 (
    .in0(3'b000), .in1(3'b001), .out(multiplexer_1_out), .sel(comparator_1_eq));  // open: en
  Multiplexer #(.width(3)) multiplexer_2 (
    .in0(3'b000), .in1(3'b010), .out(multiplexer_2_out), .sel(comparator_2_eq));  // open: en
  Multiplexer #(.width(3)) multiplexer_3 (
    .in0(3'b000), .in1(3'b011), .out(multiplexer_3_out), .sel(comparator_3_eq));  // open: en
  Multiplexer #(.width(3)) multiplexer_4 (
    .in0(3'b000), .in1(3'b100), .out(multiplexer_4_out), .sel(comparator_4_eq));  // open: en
  assign or_1_out = multiplexer_1_out | multiplexer_2_out | multiplexer_3_out | multiplexer_4_out;  // OR_Gate or_1, 3 bits wide
  Multiplexer #(.select(3), .width(9)) multiplexer_5 (
    .in0({9{1'b0}}), .in1(9'h128), .in2(9'h70), .in3(9'h102), .in4(9'h85), .out(Codigo_de_Cu), .sel(or_1_out));  // open: in5, in6, in7, en

  // Notes on the sheet:
  //   Expandir a 8 operaciones con nuestro propio comparador
endmodule

module Program_Counter (
  input  [7:0] Inmediato,
  input  Procesamos_Ints__J,
  input  Clock,
  input  Reset,
  output [7:0] \Dirección_de_Memoria_de_las_Instrucciones 
);

  wire [7:0] adder_1_out, multiplexer_1_out;

  Multiplexer #(.width(8)) multiplexer_1 (
    .in0(adder_1_out), .in1(Inmediato), .out(multiplexer_1_out), .sel(Procesamos_Ints__J));  // open: en
  Register Registro (
    .D(multiplexer_1_out), .Q(\Dirección_de_Memoria_de_las_Instrucciones ), .clk(Clock), .clr(Reset));  // open: en
  Adder adder_1 (.a(8'h1), .b(\Dirección_de_Memoria_de_las_Instrucciones ), .out(adder_1_out));  // open: cin, cout
endmodule
