// Logisim project Practica9.circ as structural Verilog: 7 circuits, main circuit main
module main (
  input  [31:0] in_1,
  input  en,
  input  next_pc,
  input  in_4,
  input  reset,
  output [31:0] out_6
);

  wire clock_1_out;
  wire [31:0] adder_1_out, multiplexer_1_out;

  Adder #(.width(32)) adder_1 (.a(out_6), .b(32'h1), .out(adder_1_out));  // open: cin, cout
  Clock clock_1 (.out(clock_1_out));
  Multiplexer #(.width(32)) multiplexer_1 (
    .in0(adder_1_out), .in1(in_1), .out(multiplexer_1_out), .sel(next_pc), .en(in_4));
  Register #(.width(32)) register_1 (.D(multiplexer_1_out), .en(en), .Q(out_6), .clk(clock_1_out), .clr(reset));

  // Notes on the sheet:
  //   pc_sel
  //   reloj
endmodule

module RAM_ROM (
  input  [7:0] in_1,
  input  en,
  input  next_pc,
  input  in_4,
  input  reset,
  input  select,
  output [31:0] out_7
);

  wire clock_1_out;
  wire [7:0] adder_1_out, multiplexer_1_out, register_1_q;
  wire [31:0] ram_1_data, rom_1_data;

  Clock clock_1 (.out(clock_1_out));
  Adder adder_1 (.a(register_1_q), .b(8'h1), .out(adder_1_out));  // open: cin, cout
  Multiplexer #(.width(8)) multiplexer_1 (
    .in0(adder_1_out), .in1(in_1), .out(multiplexer_1_out), .sel(next_pc), .en(in_4));
  Register register_1 (.D(multiplexer_1_out), .en(en), .Q(register_1_q), .clk(clock_1_out), .clr(reset));
  RAM #(.dataWidth(32)) ram_1 (.addr(register_1_q), .data(ram_1_data), .clk(clock_1_out));  // open: sel, ld, clr
  ROM #(.dataWidth(32)) rom_1 (.addr(register_1_q), .data(rom_1_data));  // open: sel
  Multiplexer #(.width(32)) multiplexer_2 (.in0(ram_1_data), .in1(rom_1_data), .out(out_7), .sel(select));  // open: en

  // Notes on the sheet:
  //   pc_sel
  //   reloj
  //   RAM
  //   ROM
  //   contents of rom_1 (hex, n*v repeats v):
  //   1 2
endmodule

module RegisterFile (
  input  en,
  input  [1:0] addr,
  input  [1:0] in_3,
  input  [31:0] in_4,
  input  [1:0] in_5,
  output [31:0] out_6,
  output [31:0] out_7
);

  wire clock_1_out, demultiplexer_1_out0, demultiplexer_1_out1, demultiplexer_1_out2, demultiplexer_1_out3;
  wire [31:0] register_1_q, register_2_q, register_3_q, register_4_q;

  Demultiplexer #(.select(2)) demultiplexer_1 (
    .out0(demultiplexer_1_out0), .out1(demultiplexer_1_out1), .out2(demultiplexer_1_out2),
    .out3(demultiplexer_1_out3), .in(en), .sel(addr));  // open: en
  Register #(.width(32)) register_1 (
    .D(in_4), .en(demultiplexer_1_out0), .Q(register_1_q), .clk(clock_1_out));  // open: clr
  Register #(.width(32)) register_2 (
    .D(in_4), .en(demultiplexer_1_out1), .Q(register_2_q), .clk(clock_1_out));  // open: clr
  Register #(.width(32)) register_3 (
    .D(in_4), .en(demultiplexer_1_out3), .Q(register_3_q), .clk(clock_1_out));  // open: clr
  Register #(.width(32)) register_4 (
    .D(in_4), .en(demultiplexer_1_out2), .Q(register_4_q), .clk(clock_1_out));  // open: clr
  Clock clock_1 (.out(clock_1_out));
  Multiplexer #(.select(2), .width(32)) multiplexer_1 (
    .in0(register_1_q), .in1(register_2_q), .in2(register_3_q), .in3(register_4_q), .out(out_6), .sel(in_3));  // open: en
  Multiplexer #(.select(2), .width(32)) multiplexer_2 (
    .in0(register_1_q), .in1(register_2_q), .in2(register_3_q), .in3(register_4_q), .out(out_7), .sel(in_5));  // open: en
endmodule

module UC (
  input  [2:0] opcode,
  output write,
  output ImmSrc0,
  output ImmSrc1,
  output AluSrc,
  output MemWrite,
  output out_7,
  output branch,
  output out_9,
  output out_10
);

  wire decoder_1_out0, decoder_1_out2, decoder_1_out3, decoder_1_out4, decoder_1_out5, decoder_1_out6,
       decoder_1_out7;

  Decoder #(.select(3), .enable("false")) decoder_1 (
    .out0(decoder_1_out0), .out1(MemWrite), .out2(decoder_1_out2), .out3(decoder_1_out3),
    .out4(decoder_1_out4), .out5(decoder_1_out5), .out6(decoder_1_out6), .out7(decoder_1_out7), .sel(opcode));
  or or_1 (write, decoder_1_out6, decoder_1_out0, decoder_1_out5, decoder_1_out2, decoder_1_out4);
  or or_2 (ImmSrc0, MemWrite, decoder_1_out2);
  or or_3 (ImmSrc1, decoder_1_out2, decoder_1_out3);
  or or_4 (AluSrc, decoder_1_out0, MemWrite, decoder_1_out5, decoder_1_out4, decoder_1_out6);
  or or_5 (out_7, decoder_1_out0, MemWrite, decoder_1_out3, decoder_1_out7);
  or or_6 (branch, decoder_1_out7, decoder_1_out3);
  or or_7 (out_9, decoder_1_out3, decoder_1_out5);
  or or_8 (out_10, decoder_1_out2, decoder_1_out6);

  // Notes on the sheet:
  //   result
  //   alu1
  //   alu2
endmodule

module ALU_INT (
  input  in_1,
  input  [31:0] A,
  input  in_3,
  input  [31:0] B,
  input  [2:0] \Operación ,
  output Cero,
  output Desborde,
  output Negativo,
  output \_0__Lógica___1__Aritmética ,
  output [31:0] Resultado
);

  wire adder_1_cout, adder_2_cout, and_2_out, not_2_out;
  wire [31:0] adder_1_out, adder_2_out, and_1_out, not_1_out, or_1_out, subtractor_1_out, subtractor_2_out;

  Adder #(.width(32)) adder_1 (.a(A), .b(B), .out(adder_1_out), .cin(in_1), .cout(adder_1_cout));
  Subtractor #(.width(32)) subtractor_1 (.a(A), .b(B), .out(subtractor_1_out));  // open: bin, bout
  Adder #(.width(32)) adder_2 (.a(A), .b(32'h1), .out(adder_2_out), .cin(in_3), .cout(adder_2_cout));
  Subtractor #(.width(32)) subtractor_2 (.a(A), .b(32'h1), .out(subtractor_2_out));  // open: bin, bout
  assign or_1_out = A | B;  // OR_Gate or_1, 32 bits wide
  assign not_1_out = ~A;  // NOT_Gate not_1, 32 bits wide
  assign and_1_out = A & B;  // AND_Gate and_1, 32 bits wide
  Multiplexer #(.select(3), .width(32), .enable("false")) multiplexer_1 (
    .in0(and_1_out), .in1(or_1_out), .in2(adder_1_out), .in3(subtractor_1_out), .in4(not_1_out),
    .in5(adder_2_out), .in6(subtractor_2_out), .in7(A), .out(Resultado), .sel(\Operación ));
  or or_2 (Desborde, adder_1_cout, adder_2_cout);
  not not_2 (not_2_out, \Operación [2]);
  and and_2 (and_2_out, \Operación [0], \Operación [1], not_2_out);
  or or_3 (\_0__Lógica___1__Aritmética , \Operación [1], \Operación [2]);
  Comparator #(.width(32)) comparator_1 (.a(Resultado), .b({32{1'b0}}), .eq(Cero));  // open: gt, lt
  and and_3 (Negativo, Resultado[31], and_2_out);

  // Notes on the sheet:
  //   000. AND
  //   001. OR
  //   010. ADD
  //   011. SUB
  //   100. NEGATE
  //   101. INCREMENT
  //   110. DECREMENT
  //   111. PASS
endmodule

module ALU_FLOAT (
  input  in_1,
  input  [31:0] A,
  input  in_3,
  input  [31:0] B,
  input  [2:0] \Operación ,
  output Cero,
  output Desborde,
  output Negativo,
  output \_0__Lógica___1__Aritmética ,
  output [31:0] Resultado
);

  wire adder_1_cout, adder_2_cout, and_2_out, not_2_out;
  wire [31:0] adder_1_out, adder_2_out, and_1_out, not_1_out, or_1_out, subtractor_1_out, subtractor_2_out;

  Adder #(.width(32)) adder_1 (.a(A), .b(B), .out(adder_1_out), .cin(in_1), .cout(adder_1_cout));
  Subtractor #(.width(32)) subtractor_1 (.a(A), .b(B), .out(subtractor_1_out));  // open: bin, bout
  Adder #(.width(32)) adder_2 (.a(A), .b(32'h1), .out(adder_2_out), .cin(in_3), .cout(adder_2_cout));
  Subtractor #(.width(32)) subtractor_2 (.a(A), .b(32'h1), .out(subtractor_2_out));  // open: bin, bout
  assign or_1_out = A | B;  // OR_Gate or_1, 32 bits wide
  assign not_1_out = ~A;  // NOT_Gate not_1, 32 bits wide
  assign and_1_out = A & B;  // AND_Gate and_1, 32 bits wide
  Multiplexer #(.select(3), .width(32), .enable("false")) multiplexer_1 (
    .in0(and_1_out), .in1(or_1_out), .in2(adder_1_out), .in3(subtractor_1_out), .in4(not_1_out),
    .in5(adder_2_out), .in6(subtractor_2_out), .in7(A), .out(Resultado), .sel(\Operación ));
  or or_2 (Desborde, adder_1_cout, adder_2_cout);
  not not_2 (not_2_out, \Operación [2]);
  and and_2 (and_2_out, \Operación [0], \Operación [1], not_2_out);
  or or_3 (\_0__Lógica___1__Aritmética , \Operación [1], \Operación [2]);
  Comparator #(.width(32)) comparator_1 (.a(Resultado), .b({32{1'b0}}), .eq(Cero));  // open: gt, lt
  and and_3 (Negativo, Resultado[31], and_2_out);

  // Notes on the sheet:
  //   000. AND
  //   001. OR
  //   010. ADD
  //   011. SUB
  //   100. NEGATE
  //   101. INCREMENT
  //   110. DECREMENT
  //   111. PASS
endmodule

module RegisterFIleFloat (
  input  en,
  input  [1:0] addr,
  input  [1:0] in_3,
  input  [31:0] in_4,
  input  [1:0] in_5,
  output [31:0] out_6,
  output [31:0] out_7
);

  wire clock_1_out, demultiplexer_1_out0, demultiplexer_1_out1, demultiplexer_1_out2, demultiplexer_1_out3;
  wire [31:0] register_1_q, register_2_q, register_3_q, register_4_q;

  Demultiplexer #(.select(2)) demultiplexer_1 (
    .out0(demultiplexer_1_out0), .out1(demultiplexer_1_out1), .out2(demultiplexer_1_out2),
    .out3(demultiplexer_1_out3), .in(en), .sel(addr));  // open: en
  Register #(.width(32)) register_1 (
    .D(in_4), .en(demultiplexer_1_out0), .Q(register_1_q), .clk(clock_1_out));  // open: clr
  Register #(.width(32)) register_2 (
    .D(in_4), .en(demultiplexer_1_out1), .Q(register_2_q), .clk(clock_1_out));  // open: clr
  Register #(.width(32)) register_3 (
    .D(in_4), .en(demultiplexer_1_out3), .Q(register_3_q), .clk(clock_1_out));  // open: clr
  Register #(.width(32)) register_4 (
    .D(in_4), .en(demultiplexer_1_out2), .Q(register_4_q), .clk(clock_1_out));  // open: clr
  Clock clock_1 (.out(clock_1_out));
  Multiplexer #(.select(2), .width(32)) multiplexer_1 (
    .in0(register_1_q), .in1(register_2_q), .in2(register_3_q), .in3(register_4_q), .out(out_6), .sel(in_3));  // open: en
  Multiplexer #(.select(2), .width(32)) multiplexer_2 (
    .in0(register_1_q), .in1(register_2_q), .in2(register_3_q), .in3(register_4_q), .out(out_7), .sel(in_5));  // open: en
endmodule
