// Logisim project XOR's.circ as structural Verilog: 3 circuits, main circuit main
module main (
  input  [3:0] in_1,
  output _0000,
  output _0001,
  output _0010,
  output _0011,
  output _0100,
  output _0101,
  output _0110,
  output _0111,
  output _1000,
  output _1001,
  output _1010,
  output _1011,
  output _1100,
  output _1101,
  output _1110,
  output _1111
);

  wire decoder_1_out0, decoder_1_out1, decoder_1_out2, decoder_1_out3;

  Decoder #(.select(2), .disabled(0)) decoder_1 (
    .out0(decoder_1_out0), .out1(decoder_1_out1), .out2(decoder_1_out2), .out3(decoder_1_out3),
    .sel(in_1[3:2]), .en(1'b1));
  Decoder #(.select(2), .disabled(0)) decoder_2 (
    .out0(_0000), .out1(_0001), .out2(_0010), .out3(_0011), .sel(in_1[1:0]), .en(decoder_1_out0));
  Decoder #(.select(2), .disabled(0)) decoder_3 (
    .out0(_0100), .out1(_0101), .out2(_0110), .out3(_0111), .sel(in_1[1:0]), .en(decoder_1_out1));
  Decoder #(.select(2), .disabled(0)) decoder_4 (
    .out0(_1000), .out1(_1001), .out2(_1010), .out3(_1011), .sel(in_1[1:0]), .en(decoder_1_out2));
  Decoder #(.select(2), .disabled(0)) decoder_5 (
    .out0(_1100), .out1(_1101), .out2(_1110), .out3(_1111), .sel(in_1[1:0]), .en(decoder_1_out3));
endmodule

module XOR_con_NAND (
  input  A,
  input  B,
  output XOR
);

  wire nand_1_out, nand_2_out, nand_3_out;

  nand nand_1 (nand_1_out, A, B);
  nand nand_2 (nand_2_out, A, nand_1_out);
  nand nand_3 (nand_3_out, nand_1_out, B);
  nand nand_4 (XOR, nand_2_out, nand_3_out);
endmodule

module XOR_con_NOR (
  input  A,
  input  B,
  output XOR
);

  wire nor_1_out, nor_2_out, nor_3_out, nor_4_out;

  nor nor_1 (nor_1_out, A, B);
  nor nor_2 (nor_2_out, A, nor_1_out);
  nor nor_3 (nor_3_out, nor_1_out, B);
  nor nor_4 (nor_4_out, nor_2_out, nor_3_out);
  nor nor_5 (XOR, nor_4_out, nor_4_out);
endmodule
