// Logisim project Automata.circ as structural Verilog: 1 circuit, main circuit main
module main (
  input  x,
  input  y,
  output S1,
  output S0
);

  wire and_1_out, and_2_out, and_3_out, and_4_out, and_5_out, clock_1_out, d_ff_1_qn, d_ff_2_qn, or_1_out,
       or_2_out;

  Clock clock_1 (.out(clock_1_out));
  and and_1 (and_1_out, x, S1);
  and and_2 (and_2_out, S0, d_ff_1_qn);
  and and_3 (and_3_out, x, d_ff_2_qn, d_ff_1_qn);
  and and_4 (and_4_out, y, S0, d_ff_1_qn);
  and and_5 (and_5_out, x, y);
  or or_1 (or_1_out, and_1_out, and_2_out);
  or or_2 (or_2_out, and_3_out, and_4_out, and_5_out);
  D_Flip_Flop d_ff_1 (.clk(clock_1_out), .D(or_1_out), .Q(S1), .Qn(d_ff_1_qn));  // open: preset, en, reset
  D_Flip_Flop d_ff_2 (.clk(clock_1_out), .D(or_2_out), .Q(S0), .Qn(d_ff_2_qn));  // open: preset, en, reset
endmodule
